# Fritzing sketch Feather_32u4_LoRa_Distance (saved by Fritzing 0.9.3b)

parts:
  Composant1 = Adafruit Feather 32u4 RFM9xW LoRa [part_number="Adafruit #3078 and Adafruit #3079"]
  Composant2 = Adafruit TPL5110 Power Timer [part_number="Adafruit #3435"]
  U1 = LIPO-110mAh [package=lipo-110]  # not connected
  Grove_Ultrasonic_Ranger1 = Grove Ultrasonic Ranger

nets:
  GND: Composant1.GND, Composant2.GND, Grove_Ultrasonic_Ranger1.GND
  +3V3: Composant1.+3V3, Grove_Ultrasonic_Ranger1.VCC
  N1: Composant1.5, Composant2.DONE
  N2: Composant1.2, Grove_Ultrasonic_Ranger1.SIG

custom parts:
  Adafruit Feather 32u4 RFM9xW LoRa: This is the Adafruit Feather 32u4 LoRa Radio (RFM9x) - our take on an microcontroller with a "Long Range (LoRa)" packet radio transceiver with built in USB and battery charging. Its an Adafruit Feather 32u4 with a 868/915 MHz radio module cooked in! Great for making wireless networks that can go further than 2.4GHz 802.15.4 and similar, are more flexible than Bluetooth LE and without the high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
  Adafruit TPL5110 Power Timer: With some development boards, low power usage is an afterthought. Especially when price and usability is the main selling point. So what should you do when its time to turn around and make that project of yours run on a battery or solar? Sure you could try to hot-air that regulator off, or you could jerry-rig a relay. Or, use a 555? Ugh, the options aren't that great. The Adafruit TPL5110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
  Grove Ultrasonic Ranger: Ultrasonic Ranger, Grove connector.
